# Fritzing sketch Arduino Temperature Control (saved by Fritzing 0.7.12b)
breadboards: 1

parts:
  Arduino1 = Arduino
  S1 = Pushbutton [package="[THT]"]
  S2 = Pushbutton [package="[THT]"]
  R1 = Resistor [tolerance=±5% resistance=10k package=THT]
  R2 = Resistor [tolerance=±5% resistance=10k package=THT]
  LCD1 = LCD screen
  R3 = Rotary Potentiometer (Small) [maximum_resistance=100kΩ]
  S3 = Tilt Switch [package=THT]
  R4 = Resistor [tolerance=±5% resistance=220 package=THT]
  R5 = Resistor [tolerance=±5% resistance=10k package=THT]

nets:
  N1: Arduino1.aref, Arduino1.3V3, R4.Pin_0
  N2: Arduino1.D12, LCD1.RS
  N3: Arduino1.D11, LCD1.E
  N4: Arduino1.D9, S3.Pin_1
  N5: Arduino1.D7, S2.Pin_1, S2.Pin_2, R2.Pin_1
  N6: Arduino1.D6, S1.Pin_1, S1.Pin_2, R1.Pin_1
  N7: Arduino1.D5, LCD1.DB4
  N8: Arduino1.D4, LCD1.DB5
  N9: Arduino1.D3, LCD1.DB6
  N10: Arduino1.D2, LCD1.DB7
  N11: Arduino1.GND, R5.Pin_1
  N12: Arduino1.A0, R4.Pin_1
  N13: S1.Pin_3, S1.Pin_4, S2.Pin_3, S2.Pin_4, LCD1.VDD, R3.leg2
  N14: R1.Pin_0, R2.Pin_0, LCD1.VSS, LCD1.R/W, R3.leg1, S3.Pin_2
  N15: LCD1.V0, R3.wiper

notes:
  Powerswitch Tail
  503 Temperature Resistor
